# Fritzing sketch uncompressed_omnipresense_drawn (saved by Fritzing 0.9.3b)

parts:
  Part1 = Arduino Due (Rev2b)
  U1 = ops283 [chip_label=IC]

nets:
  N1: Part1.D18/TX1, U1.connector4
  N2: Part1.D19/RX1, U1.connector3
  N3: Part1.5V, U1.connector1
  N4: Part1.GND, U1.connector0
